// Logisim project Sea Battle.circ as structural Verilog
module Sea_Battle (
  input  N1,
  input  N2,
  input  N3,
  input  N4,
  input  M1,
  input  M2,
  input  M3,
  input  M4,
  input  U1,
  input  U2,
  input  U3,
  input  U4,
  output HIT,
  output MISS
);

  wire and_1_out, and_2_out, and_3_out, and_4_out, and_5_out, and_6_out, and_7_out, and_8_out, and_9_out,
       and_10_out, and_11_out, and_12_out, and_13_out, and_14_out, and_15_out, and_16_out, and_17_out,
       and_18_out, and_19_out, and_20_out, and_21_out, and_22_out, and_23_out, and_24_out, and_25_out,
       and_26_out, and_27_out, and_28_out, and_29_out, and_30_out, and_31_out, and_32_out, D_out, nor_1_out,
       not_1_out, not_2_out, not_3_out, not_4_out, not_5_out, not_6_out, not_7_out, not_8_out, not_9_out,
       not_10_out, not_11_out, not_12_out, not_13_out, not_14_out, not_15_out, not_16_out, not_17_out,
       not_18_out, not_19_out, not_20_out, not_21_out, not_22_out, not_23_out, not_24_out, not_25_out,
       not_26_out, not_27_out, not_28_out, not_29_out, not_30_out, not_31_out, not_32_out, not_33_out,
       not_34_out, not_35_out, not_36_out, not_37_out, not_38_out, not_39_out, not_40_out, not_41_out,
       not_42_out, not_43_out, not_44_out, or_1_out, or_2_out, or_3_out, or_4_out, or_5_out, or_6_out,
       or_7_out, or_8_out, xnor_1_out, xnor_2_out, xnor_3_out, xnor_4_out, xnor_5_out, xnor_6_out,
       xnor_7_out, xnor_8_out;

  Button D (.out(D_out));
  and and_1 (and_1_out, N3, N4);
  and and_2 (and_2_out, N2, not_1_out, not_2_out);
  not not_1 (not_1_out, N3);
  not not_2 (not_2_out, N4);
  and and_3 (and_3_out, N1, N2);
  not not_3 (not_3_out, N1);
  and and_4 (and_4_out, not_3_out, not_4_out);
  not not_4 (not_4_out, N3);
  and and_5 (and_5_out, N2, N3, not_5_out);
  not not_5 (not_5_out, N4);
  and and_6 (and_6_out, N1, N3, N4);
  not not_6 (not_6_out, N3);
  not not_7 (not_7_out, N4);
  not not_8 (not_8_out, N1);
  not not_9 (not_9_out, N2);
  not not_10 (not_10_out, N1);
  not not_11 (not_11_out, N3);
  not not_12 (not_12_out, N4);
  not not_13 (not_13_out, N1);
  not not_14 (not_14_out, N2);
  not not_15 (not_15_out, N3);
  not not_16 (not_16_out, N1);
  not not_17 (not_17_out, N2);
  not not_18 (not_18_out, N4);
  not not_19 (not_19_out, N3);
  not not_20 (not_20_out, N4);
  not not_21 (not_21_out, N1);
  not not_22 (not_22_out, N2);
  not not_23 (not_23_out, M3);
  not not_24 (not_24_out, M4);
  not not_25 (not_25_out, M1);
  not not_26 (not_26_out, M3);
  not not_27 (not_27_out, M4);
  not not_28 (not_28_out, M3);
  not not_29 (not_29_out, M4);
  not not_30 (not_30_out, M1);
  not not_31 (not_31_out, M2);
  not not_32 (not_32_out, M1);
  not not_33 (not_33_out, M3);
  not not_34 (not_34_out, M4);
  not not_35 (not_35_out, M1);
  not not_36 (not_36_out, M2);
  not not_37 (not_37_out, M3);
  not not_38 (not_38_out, M1);
  not not_39 (not_39_out, M2);
  not not_40 (not_40_out, M4);
  not not_41 (not_41_out, M3);
  not not_42 (not_42_out, M4);
  not not_43 (not_43_out, M1);
  not not_44 (not_44_out, M2);
  or or_1 (or_1_out, and_1_out, and_2_out, and_3_out);
  or or_2 (or_2_out, and_4_out, and_5_out, and_6_out);
  and and_7 (and_7_out, not_6_out, not_7_out);
  and and_8 (and_8_out, not_8_out, not_9_out, N3, N4);
  and and_9 (and_9_out, not_10_out, N2, not_11_out);
  and and_10 (and_10_out, N1, not_12_out);
  and and_11 (and_11_out, not_13_out, not_14_out, not_15_out);
  and and_12 (and_12_out, not_16_out, not_17_out, not_18_out);
  and and_13 (and_13_out, not_19_out, not_20_out);
  and and_14 (and_14_out, not_21_out, N2, N3, N4);
  and and_15 (and_15_out, N1, not_22_out, N3, N4);
  and and_16 (and_16_out, M3, M4);
  and and_17 (and_17_out, M2, not_23_out, not_24_out);
  or or_3 (or_3_out, and_16_out, and_17_out, and_18_out);
  and and_18 (and_18_out, M1, M2);
  and and_19 (and_19_out, not_25_out, not_26_out);
  or or_4 (or_4_out, and_19_out, and_20_out, and_21_out);
  and and_20 (and_20_out, M2, M3, not_27_out);
  and and_21 (and_21_out, M1, M3, M4);
  and and_22 (and_22_out, not_28_out, not_29_out);
  and and_23 (and_23_out, not_30_out, not_31_out, M3, M4);
  and and_24 (and_24_out, not_32_out, M2, not_33_out);
  and and_25 (and_25_out, M1, not_34_out);
  and and_26 (and_26_out, not_35_out, not_36_out, not_37_out);
  and and_27 (and_27_out, not_38_out, not_39_out, not_40_out);
  and and_28 (and_28_out, not_41_out, not_42_out);
  and and_29 (and_29_out, not_43_out, M2, M3, M4);
  and and_30 (and_30_out, M1, not_44_out, M3, M4);
  or or_5 (or_5_out, and_7_out, and_8_out, and_9_out, and_10_out);
  or or_6 (or_6_out, and_11_out, and_12_out, and_13_out, and_14_out, and_15_out);
  or or_7 (or_7_out, and_22_out, and_23_out, and_24_out, and_25_out);
  or or_8 (or_8_out, and_26_out, and_27_out, and_28_out, and_29_out, and_30_out);
  xnor xnor_1 (xnor_1_out, or_1_out, U1);
  xnor xnor_2 (xnor_2_out, or_2_out, U2);
  xnor xnor_3 (xnor_3_out, or_5_out, U3);
  xnor xnor_4 (xnor_4_out, or_6_out, U4);
  xnor xnor_5 (xnor_5_out, U1, or_3_out);
  xnor xnor_6 (xnor_6_out, U2, or_4_out);
  xnor xnor_7 (xnor_7_out, U3, or_7_out);
  xnor xnor_8 (xnor_8_out, U4, or_8_out);
  and and_31 (and_31_out, xnor_1_out, xnor_2_out, xnor_3_out, xnor_4_out, D_out);
  and and_32 (and_32_out, xnor_5_out, xnor_6_out, xnor_7_out, xnor_8_out, D_out);
  nor nor_1 (nor_1_out, and_31_out, and_32_out);
  or or_9 (HIT, and_31_out, and_32_out);
  and and_33 (MISS, nor_1_out, D_out);
endmodule
