// Logisim project a.circ as structural Verilog
module _1 (
  input  A,
  input  B,
  input  C,
  input  D,
  output S
);

  wire and_1_out, or_1_out, xnor_1_out;

  and and_1 (and_1_out, A, B);
  xnor xnor_1 (xnor_1_out, and_1_out, C);
  or or_1 (or_1_out, xnor_1_out, D);
  nand nand_1 (S, or_1_out, C);
endmodule
